# Fritzing sketch Sketch (saved by Fritzing 0.9.3b)

parts:
  Part1 = Arduino Uno (Rev3)
  L298N1 = L298N DC motor driver
  M2 = DC Motor
  M3 = DC Motor
  Part2 = SRF05 Ultrasonic Rangefinder
  Part3 = Bluetooth HC-05 Macho
  S1 = Round Pushbutton
  VCC1 = Battery block 9V  # not connected

nets:
  N1: Part1.A0, L298N1.IN4
  N2: Part1.A1, L298N1.IN3
  N3: Part1.A2, L298N1.IN2
  N4: Part1.A3, L298N1.IN1
  N5: Part1.D10_PWM/SS, L298N1.ENA
  N6: Part1.D11_PWM/MOSI, L298N1.ENB
  N7: Part1.D0/RX, Part3.TXD
  N8: Part1.D1/TX, Part3.RXD
  N9: Part1.D4, Part3.State
  N10: Part1.D6_PWM, Part2.Echo
  N11: Part1.D7, Part2.Trig
  5V: Part1.5V, L298N1.5V, Part2.VCC, Part3.VCC
  GND: Part1.GND, Part2.GND, Part3.GND
  N12: L298N1.OUT1, M2.pin_2
  N13: L298N1.OUT2, M2.pin_1
  N14: L298N1.OUT3, M3.pin_2
  N15: L298N1.OUT4, M3.pin_1
  N16: L298N1.12V, S1.leg1

custom parts:
  L298N DC motor driver: 2x DC motor driver with 78M05 positive voltage regulator (7..35 V) L298N: max 46 V, 2 A Set 5 V Enable jumper to enable 5 V regultor (needed for the L298N) and +5 V output at screw terminal or supply external +5 V at screw terminal Set ENA and/or ENB to +5 V to enable motor permanently or supply ENA and/or ENB with PWM signal IN1 and IN2 set rotation directory for motor A (OUT1/OUT2) IN2 and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

// code stored in the sketch: Fritzing.ino
// Pin 1(RX) & Pin 2(TX) used for Serial -> Bluetooth

//     -- Sonar --
const int trigPin = 7, echoPin = 6;     // For ultrasound sensor
int distance = -1;
bool isDistanceSent = false;

const int loopPeriod = 250;    // a period of 250ms = a frequency of 4Hz || Checks distance in every -> loopPeriod
unsigned long timeLoopDelay = 0;

//     -- Motor --
const int enA = 10, in1 = A3, in2 = A2;      // Motor A connections
const int enB = 11, in3 = A1, in4 = A0;      // Motor B connections
int motorDirection = 0, motorSpeed = 0, motorRunFor = 3;

bool isSpeechDelayDone = false;

void setup() {
  //     -- Sonar --
  pinMode(trigPin, OUTPUT);
  pinMode(echoPin, INPUT);

  //     -- Motor --
  pinMode(enA, OUTPUT);
  pinMode(enB, OUTPUT);
  pinMode(in1, OUTPUT);
  pinMode(in2, OUTPUT);
  pinMode(in3, OUTPUT);
  pinMode(in4, OUTPUT);

  Serial.begin(9600);
}

void loop() {
  isDistanceSent = false;

  if (isSpeechDelayDone) {
    Stop();
    isSpeechDelayDone = false;
  }
  
  if (Serial.available()) {
    String command = Serial.readStringUntil('#');
    if (command.length() == 4) {
      motorDirection = command.substring(0, 1).toInt();
      Stop();
      
      if (motorDirection <= 4) {
        // Joystick / Gesture control
        motorSpeed = command.substring(1, 4).toInt();       // speed (0-100)
        motorSpeed = map(motorSpeed, 0, 100, 70, 255);
        setMotorSpeed(motorSpeed);
        
        switch (motorDirection) {
          case 1:
            forward();
            break;
          case 2:
            right();
            break;
          case 3:
            backward();
            break;
          case 4:
            left();
            break;
        }
        sendDistanceAndWait(10);
        isDistanceSent = true;
      }
      else {
        // Voice control
        motorRunFor = command.substring(1, 4).toInt();      // delay time (second)
        setMotorSpeed(255);
        
        switch (motorDirection) {
          case 5:
            forward();
            break;
          case 6:
            right();
            break;
          case 7:
            backward();
            break;
          case 8:
            left();
            break;
        }
        sendDistanceAndWait(motorRunFor * 1000);
        isDistanceSent = true;

        isSpeechDelayDone = true;
      }
    }
  }
  
  if (!isDistanceSent) sendDistance();
}

float getDistance() {
  // Returns distance in cm
  /*  Sends out an 8 cycle sonic burst from the transmitter (Trig Pin),
      which then bounces of an object and hits the receiver (Echo Pin)  */
  digitalWrite(trigPin, LOW); 
  delayMicroseconds(2); 
  digitalWrite(trigPin, HIGH); 
  delayMicroseconds(10); 
  digitalWrite(trigPin, LOW); 
  
  float duration = pulseIn(echoPin, HIGH);
  return (duration*.0343)/2;
}

void sendDistance() {
  // Checks distance every 250ms
  if (millis() - timeLoopDelay >= loopPeriod) {
    distance = round(getDistance());
    timeLoopDelay = millis();
  }

  if (distance != -1) {
    int len = String(distance).length();
    if (len < 4) {
      Serial.print("abc"[len - 1]);
      Serial.print(distance);
      Serial.print('#');
    }
  }
}

void sendDistanceAndWait(int ms) {
  unsigned long timeStart = millis();
  while (millis() - timeStart <= ms) {
    sendDistance();
  }
}

void Stop() {
  digitalWrite(in1, LOW);
  digitalWrite(in2, LOW);
  digitalWrite(in3, LOW);
  digitalWrite(in4, LOW);
}

void forward() {
  digitalWrite(in1, HIGH);
  digitalWrite(in2, LOW);
  digitalWrite(in3, HIGH);
  digitalWrite(in4, LOW);
}

void backward() {
  digitalWrite(in1, LOW);
  digitalWrite(in2, HIGH);
  digitalWrite(in3, LOW);
  digitalWrite(in4, HIGH);
}

void left() {
  digitalWrite(in1, LOW);
  digitalWrite(in2, LOW);
  digitalWrite(in3, HIGH);
  digitalWrite(in4, LOW);
}

void right() {
  digitalWrite(in1, HIGH);
  digitalWrite(in2, LOW);
  digitalWrite(in3, LOW);
  digitalWrite(in4, LOW);
}

void setMotorSpeed(int value) {
  // PWM(0-255)
  analogWrite(enA, value);
  analogWrite(enB, value);
}
